# Fritzing sketch Fermentation_Box_v3 (saved by Fritzing 0.9.4)
breadboards: 1
perfboards: 1

parts:
  part = Adafruit Pro Trinket 3.3V 12MHz [part_number="Adafruit #2010"]
  part_2 = Adafruit BME280
  M1 = RioRand LM2596
  DC_24V6A = Power plug
  Pad1 = Pad [width=22.405802711473658 height=13.119002566451892 connect=center]  # not connected
  Pad2 = Pad [width=22.405802711473658 height=13.119002566451892 connect=center]  # not connected
  U2 = TOUCH [package=touch1]
  U3 = TOUCH [package=touch1]
  U4 = TOUCH [package=touch1]
  PWM_Humidifier = IFR520 MOS module [package=THT]
  PWM_Heating_Element = IFR520 MOS module [package=THT]
  Bauteil4 = Adafruit MPR121

nets:
  N1: part.GND, M1.Pin_4
  N2: part.VBUS, M1.Pin_3
  3.3V/VCC: part.+3V3, part_2.3.3V, PWM_Humidifier.VCC, PWM_Heating_Element.VCC, Bauteil4.3.3V
  RST: part.D8
  BUSY: part.D6
  N3: part.D4, PWM_Humidifier.SIG
  N4: part.D3, PWM_Heating_Element.SIG
  DC: part.D9
  CS: part.D10
  DIN: part.D11
  CLK: part.D13
  N5: part.A4, part_2.SDI/SDA, Bauteil4.SDA
  N6: part.A5, part_2.SCK/SCL, Bauteil4.SCL
  GND: part_2.GND, PWM_Humidifier.GND, PWM_Heating_Element.GND, Bauteil4.GND
  N7: M1.Pin_1, DC_24V6A.VCC
  N8: M1.Pin_2, DC_24V6A.GND
  N9: U2.T1, Bauteil4.ELEC0
  N10: U3.T1, Bauteil4.ELEC1
  N11: U4.T1, Bauteil4.ELEC2
  5V: PWM_Humidifier.VIN
  24V: PWM_Heating_Element.VIN

notes:
  Heizkabel relay
  humidifyer relay
  Display
  Ok-Button
  (+)-Button
  (-)-Button
  2.9inch e-Paper Module
  SCL
  SDA
  Fermentation Station, 2.0

custom parts:
  Adafruit Pro Trinket 3.3V 12MHz: rinket's got a big sister in town - the Pro Trinket 3V! Pro Trinket combines everything you love about Trinket with the familiarity of the core Arduino chip, the ATmega328. It's like an Arduino Pro Mini with more pins and USB tossed in. Trinket's a year old now, and while its been great to see tons of tiny projects, sometimes you just need more pins, more FLASH, and more RAM. That's why we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
  Adafruit BME280: Bosch has stepped up their game with their new BME280 sensor, an environmental sensor with temperature, barometric pressure and humidity! This sensor is great for all sorts of weather/environmental sensing and can even be used in both I2C and SPI! This precision sensor from Bosch is the best low-cost sensing solution for measuring humidity with ±3% accuracy, barometric pressure with ±1 hPa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
  Adafruit MPR121: Add lots of touch sensors to your next microcontroller project with this easy-to-use 12-channel capacitive touch sensor breakout board, starring the MPR121. This chip can handle up to 12 individual touch pads. The MPR121 has support for only I2C, which can be implemented with nearly any microcontroller. You can select one of 4 addresses with the ADDR pin, for a total of 48 capacitive touch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
